# Fritzing sketch tricot-malin-schematic (saved by Fritzing 0.9.1b)
breadboards: 1

parts:
  Componente2 = 9DOF Sensor LSM9DS0
  Componente3 = 9DOF Sensor LSM9DS0
  NEOPIXEL1 = Neopixel Strip -- Black (30/m)
  NEOPIXEL2 = Neopixel Strip -- Black (30/m)
  Componente4 = LilyPad Buzzer
  Componente1 = JeeNode wireless microcontroller
  BLE_MINI1 = BLE Mini
  U1 = LIPO-110mAh [package=lipo-110]

nets:
  GND: Componente2.SDOG, Componente2.SDOXM, Componente2.GND, Componente3.GND, NEOPIXEL1.GND, NEOPIXEL2.GND, Componente4.-, Componente1.GND, BLE_MINI1.GND, U1.-
  N1: Componente2.SCL, Componente3.SCL, Componente1.SCL
  N2: Componente2.SDA, Componente3.SDA, Componente1.SDA
  VDD: Componente2.VDD, Componente3.VDD, NEOPIXEL1.+5V, NEOPIXEL2.+5V, Componente1.VCC, BLE_MINI1.VIN
  N3: NEOPIXEL1.Din, Componente1.DIO3
  N4: NEOPIXEL2.Din, Componente1.DIO2
  N5: Componente4.+, Componente1.DIO1
  N6: Componente1.PWX, U1.+
  N7: Componente1.RXD, BLE_MINI1.TX
  N8: Componente1.TXD, BLE_MINI1.RX

custom parts:
  9DOF Sensor LSM9DS0: This is the LSM9DS0, a versatile motion-sensing system-in-a-chip that houses a 3-axis accelerometer, 3-axis gyroscope, and 3-axis magnetometer. That’s right, 9 degrees of freedom (9dof) from a single IC! Each sensor in the LSM9DS0 supports a wide range of, well, ranges: the accelerometer’s scale can be set to ± 2, 4, 6, 8, or 16 g, the gyroscope supports ± 245, 500, and 2000 °/s, and the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
  Neopixel Strip -- Black (30/m): These NeoPixel strips have 30 digitally-addressable pixel LEDs per meter and are very affordable and are only 12.5 mm wide, 10 mm if you remove the strip from the casing.
  BLE Mini: You can now incorporate Bluetooth 4.0 Low Energy (BLE) technology easily in your project with our BLE Mini. BLE Mini requires only a serial port for communication so it supports all major development platforms that have UART interface including Arduino, Raspberry Pi, Netduino, BeagleBone etc. In addition, we provide you with access to all Ti's CC2540 I/O pins and the ability to upload firmware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
